// Logisim project DLD lab3.circ as structural Verilog: 1 circuit, main circuit main
module main (
  input  w,
  input  x,
  input  y,
  input  z,
  input  w_2,
  input  x_2,
  input  y_2,
  input  z_2,
  output out_9,
  output out_10
);

  wire and_1_out, and_2_out, and_3_out, and_4_out, not_1_out, not_2_out, not_3_out, not_4_out, not_5_out,
       not_6_out, not_7_out, or_1_out, or_2_out, or_3_out;

  not not_1 (not_1_out, w_2);
  not not_2 (not_2_out, x_2);
  not not_3 (not_3_out, y_2);
  not not_4 (not_4_out, z_2);
  not not_5 (not_5_out, w);
  not not_6 (not_6_out, y);
  not not_7 (not_7_out, z);
  or or_1 (or_1_out, w_2, not_2_out, not_3_out);
  or or_2 (or_2_out, not_1_out, y_2, not_4_out);
  or or_3 (or_3_out, z_2, x_2);
  and and_1 (and_1_out, z, not_5_out);
  and and_2 (and_2_out, w, x, not_7_out);
  and and_3 (and_3_out, not_5_out, x, not_6_out);
  and and_4 (and_4_out, y, z);
  and and_5 (out_10, or_1_out, or_2_out, or_3_out);
  or or_4 (out_9, and_1_out, and_2_out, and_3_out, and_4_out, and_4_out);

  // Notes on the sheet:
  //   F(w, x, y, z) = (x+z)(w+x'+y')(w'+y+z')
  //   F(w, x, y, z) = w'z+yz+wxz'+w'xy'
endmodule
