// Logisim project DLD lab4.circ as structural Verilog: 1 circuit, main circuit main
module main (
  input  w,
  input  x,
  input  y,
  input  z,
  output out_5
);

  wire and_1_out, and_2_out, and_3_out, and_4_out, not_1_out, not_2_out, not_3_out, not_4_out, or_1_out,
       or_2_out;

  not not_1 (not_1_out, w);
  not not_2 (not_2_out, x);
  not not_3 (not_3_out, y);
  not not_4 (not_4_out, z);
  or or_1 (or_1_out, not_2_out, y);
  and and_1 (and_1_out, x, not_3_out, z);
  and and_2 (and_2_out, or_1_out, not_4_out);
  or or_2 (or_2_out, and_1_out, and_2_out);
  and and_3 (and_3_out, not_1_out, or_2_out);
  and and_4 (and_4_out, z, not_2_out, w);
  or or_3 (out_5, and_3_out, and_4_out);

  // Notes on the sheet:
  //   F = w'.(x.y.z+z'.(x'+y))+(w.x'.z)
endmodule
