// Logisim project POS with NORs.circ as structural Verilog
module POS_with_NORs (
  input  X,
  input  Y,
  input  Z,
  input  in_4,
  input  in_5,
  input  in_6,
  output out_7,
  output out_8
);

  wire nor_1_out, nor_2_out, nor_3_out, not_1_out, not_2_out, not_3_out, or_1_out, or_2_out, or_3_out;

  not not_1 (not_1_out, in_4);
  not not_2 (not_2_out, in_5);
  not not_3 (not_3_out, X);
  or or_1 (or_1_out, in_5, in_6, not_1_out);
  or or_2 (or_2_out, not_2_out, in_6);
  or or_3 (or_3_out, in_6, in_4);
  and and_1 (out_8, or_1_out, or_2_out, or_3_out);
  nor nor_1 (nor_1_out, not_3_out, Y);
  nor nor_2 (nor_2_out, Z, not_3_out, Y);
  nor nor_3 (nor_3_out, nor_1_out, Z);
  nor nor_4 (out_7, nor_3_out, nor_2_out);

  // Notes on the sheet:
  //   ((Z+(X'+Y)')'+(X'+Y+Z)')'
endmodule
